# Fritzing sketch magic8ball (saved by Fritzing 1.0.0rc)

parts:
  A1 = Waveshare ESP32-S3 lcd
  Part1 = Adafruit MAX9814 Electret Microphone Amplifier [part_number="Adafruit #1713"]
  MOTOR1 = Vibration Motor
  MOTOR2 = Vibration Motor
  Part2 = Lithium Ion Polymer Battery 3.7v 1200mAh [part_number=258]
  Part3 = Adafruit Breadboard-Friendly NeoPixel [part_number="Adafruit #1312"]
  D1 = Diode [package=diode-1n4001]
  D2 = Diode [package=diode-1n4001]
  Q2 = NPN-Transistor [package="TO92 [THT]"]
  Q1 = NPN-Transistor [package="TO92 [THT]"]
  R1 = Resistor [tolerance=±5% resistance=1k package="0805 [SMD]"]
  R2 = Resistor [tolerance=±5% resistance=1k package="0805 [SMD]"]
  U1 = SWITCH_SPDT [package=kps-1290]

nets:
  GND: A1.Pin_20, A1.Pin_22, A1.Pin_32, A1.Pin_42, Part1.GND, MOTOR2.NEG, Part2.negative, Part3.GND, D2.A
  N1: A1.Pin_21, U1.O
  N2: A1.Pin_23, R2.Pin_1
  N3: A1.Pin_33, R1.Pin_1
  N4: A1.Pin_35, Part3.IN
  N5: A1.Pin_36, Part1.OUTPUT
  VDD: A1.Pin_41, Part1.VDD, Part3.VDD
  N6: MOTOR1.POS, D1.C, Q1.C
  N7: MOTOR1.NEG, D1.A
  N8: MOTOR2.POS, D2.C, Q2.C
  N9: Part2.positive, U1.P

custom parts:
  Waveshare ESP32-S3 lcd: ESP32-S3 Development Board, 32-bit LX7 Dual-core Processor, Integrates GC9A01 Display Driver Chip, With 1.28inch IPS Round LCD.
  Adafruit MAX9814 Electret Microphone Amplifier: Add an ear to your project with this well-designed electret microphone amplifier with AGC. This fully assembled and tested board comes with a 20-20KHz electret microphone soldered on. For the amplification, we use the Maxim MAX9814, a specialty chip that is designed for amplifying electret microphones in situations where the loudness of the audio isn't predictable. This fancy microphone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
  Vibration Motor: An eccentric vibration motor!
  Lithium Ion Polymer Battery 3.7v 1200mAh: Lithium ion polymer (also known as 'lipo' or 'lipoly') batteries are thin, light and powerful. The output ranges from 4.2V when completely charged to 3.7V. This battery has a capacity of 1200mAh for a total of about 4.5 Wh. The batteries come pre-attached with a genuine 2-pin JST-PH connector as shown and include the necessary protection circuitry.
  Adafruit Breadboard-Friendly NeoPixel: This is the easiest way possible to add small, bright RGB pixels to your project. We took the same technology from our Flora NeoPixels and made them breadboard friendly, with two rows of 3 x 0.1" spaced header on each side for easy soldering, chaining and breadboarding. These ultra-bright LEDs have a constant-current driver cooked right into the LED package! The pixels are chainable - so you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
