# Fritzing sketch magic8ball (saved by Fritzing 1.0.0rc)

parts:
  A1 = Waveshare ESP32-S3 lcd
  Part1 = Adafruit MAX9814 Electret Microphone Amplifier [part_number="Adafruit #1713"]
  MOTOR1 = Vibration Motor
  MOTOR2 = Vibration Motor
  Part2 = Lithium Ion Polymer Battery 3.7v 1200mAh [part_number=258]

nets:
  N1: A1.Pin_20, A1.Pin_22, Part2.negative
  N2: A1.Pin_21, Part2.positive
  N3: A1.Pin_33, MOTOR2.POS
  N4: A1.Pin_34, MOTOR1.POS
  N5: A1.Pin_36, Part1.OUTPUT
  N6: A1.Pin_41, Part1.VDD
  N7: Part1.GND, MOTOR2.NEG

custom parts:
  Waveshare ESP32-S3 lcd: ESP32-S3 Development Board, 32-bit LX7 Dual-core Processor, Integrates GC9A01 Display Driver Chip, With 1.28inch IPS Round LCD.
  Adafruit MAX9814 Electret Microphone Amplifier: Add an ear to your project with this well-designed electret microphone amplifier with AGC. This fully assembled and tested board comes with a 20-20KHz electret microphone soldered on. For the amplification, we use the Maxim MAX9814, a specialty chip that is designed for amplifying electret microphones in situations where the loudness of the audio isn't predictable. This fancy microphone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
  Vibration Motor: An eccentric vibration motor!
  Lithium Ion Polymer Battery 3.7v 1200mAh: Lithium ion polymer (also known as 'lipo' or 'lipoly') batteries are thin, light and powerful. The output ranges from 4.2V when completely charged to 3.7V. This battery has a capacity of 1200mAh for a total of about 4.5 Wh. The batteries come pre-attached with a genuine 2-pin JST-PH connector as shown and include the necessary protection circuitry.
